# Fritzing sketch CajaDomotica_Fija (saved by Fritzing 1.0.1rc)
breadboards: 2

parts:
  LED1 = smd LED [color="Red (633nm)" package="0603 [SMD]"]
  R1 = Resistor [tolerance=±5% power=0.25W resistance=330 package=THT]
  Q1 = NPN-Transistor [package="TO92 [THT]"]
  R2 = Resistor [tolerance=±5% power=0.25W resistance=10k package=THT]
  Q2 = NPN-Transistor [package="TO92 [THT]"]
  R4 = Resistor [tolerance=±5% power=0.25W resistance=330 package=THT]
  R5 = Resistor [tolerance=±5% power=0.25W resistance=10k package=THT]
  KY-1 = Keyes Relay [package=THT]
  KY-2 = Keyes Relay [package=THT]
  S1 = Pushbutton [package="[THT]"]
  KY-3 = Keyes Relay [package=THT]
  KY-4 = Keyes Relay [package=THT]
  Q3 = NPN-Transistor [package="TO92 [THT]"]
  Q4 = NPN-Transistor [package="TO92 [THT]"]
  R7 = Resistor [tolerance=±5% power=0.25W resistance=330 package=THT]
  R8 = Resistor [tolerance=±5% power=0.25W resistance=330 package=THT]
  R9 = Resistor [tolerance=±5% power=0.25W resistance=10k package=THT]
  R10 = Resistor [tolerance=±5% power=0.25W resistance=10k package=THT]
  R11 = Resistor [tolerance=±5% power=0.25W resistance=330 package=THT]
  LED2 = smd LED [color="Red (633nm)" package="0603 [SMD]"]
  LED3 = smd LED [color="Red (633nm)" package="0603 [SMD]"]
  LED4 = smd LED [color="Red (633nm)" package="0603 [SMD]"]
  LED5 = smd LED [color="Blue (430nm)" package="0603 [SMD]"]
  R12 = Resistor [tolerance=±5% power=0.25W resistance=330 package=THT]
  R13 = Resistor [tolerance=±5% power=0.25W resistance=330 package=THT]
  R14 = Resistor [tolerance=±5% power=0.25W resistance=330 package=THT]
  R15 = Resistor [tolerance=±5% power=0.25W resistance=330 package=THT]
  R16 = Resistor [tolerance=±5% power=0.25W resistance=10k package=THT]  # not connected
  R17 = Resistor [tolerance=±5% power=0.25W resistance=10k package=THT]
  S2 = Pushbutton [package="[THT]"]
  S3 = Pushbutton [package="[THT]"]
  S4 = Pushbutton [package="[THT]"]
  S5 = Pushbutton [package="[THT]"]
  R18 = Resistor [tolerance=±5% power=0.25W resistance=10k package=THT]
  R19 = Resistor [tolerance=±5% power=0.25W resistance=10k package=THT]
  R20 = Resistor [tolerance=±5% power=0.25W resistance=10k package=THT]
  R21 = Resistor [tolerance=±5% power=0.25W resistance=10k package=THT]
  M1 = DOIT Esp32 DevKit v1 (30 pins long, 11 pins width) [part_number=ESP32S-PIN30]

nets:
  N1: LED1.cathode, R11.Pin_1
  N2: LED1.anode, M1.TX0
  N3: R1.Pin_0, M1.D13
  N4: R1.Pin_1, Q1.B
  N5: Q1.E, Q2.E, KY-1.ground, KY-2.ground, KY-3.ground, KY-4.ground, Q3.E, R11.Pin_0, R12.Pin_0, R13.Pin_0, R14.Pin_0, R15.Pin_0, R17.Pin_0, S5.Pin_3, S5.Pin_4, R18.Pin_0, R19.Pin_0, R21.Pin_0, M1.GND
  N6: Q1.C, R2.Pin_1, KY-1.signal
  N7: R2.Pin_0, R5.Pin_0, KY-1.power, KY-2.power, KY-3.power, KY-4.power, Q4.E, R9.Pin_0, R10.Pin_0, M1.VIN
  N8: Q2.B, R4.Pin_1
  N9: Q2.C, R5.Pin_1, KY-2.signal
  N10: R4.Pin_0, M1.D18
  N11: S1.Pin_1, S1.Pin_2, R17.Pin_1, M1.D25
  N12: S1.Pin_3, S1.Pin_4, S2.Pin_3, S2.Pin_4, S3.Pin_3, S3.Pin_4, S4.Pin_3, S4.Pin_4, R20.Pin_0, M1.3V3
  N13: KY-3.signal, Q3.C, R9.Pin_1
  N14: KY-4.signal, Q4.C, R10.Pin_1
  N15: Q3.B, R7.Pin_1
  N16: Q4.B, R8.Pin_1
  N17: R7.Pin_0, M1.D19
  N18: R8.Pin_0, M1.D4
  N19: LED2.cathode, R12.Pin_1
  N20: LED2.anode, M1.D5
  N21: LED3.cathode, R13.Pin_1
  N22: LED3.anode, M1.D14
  N23: LED4.cathode, R14.Pin_1
  N24: LED4.anode, M1.D27
  N25: LED5.cathode, R15.Pin_1
  N26: LED5.anode, M1.D26
  N27: S2.Pin_1, S2.Pin_2, R18.Pin_1, M1.D33
  N28: S3.Pin_1, S3.Pin_2, R19.Pin_1, M1.D35
  N29: S4.Pin_1, S4.Pin_2, R21.Pin_1, M1.D34
  N30: S5.Pin_1, S5.Pin_2, R20.Pin_1, M1.D32

custom parts:
  Keyes Relay: The Keyes 5V relay module is suitable for SCM development, home appliance control. It uses a 5V~12V TIL control signal which can control DC / AC signal.
  DOIT Esp32 DevKit v1 (30 pins long, 11 pins width): The DOIT Esp32 DevKit v1 is one of the development board created by DOIT to evaluate the ESP-WROOM-32 module. It is based on the ESP32 microcontroller that boasts Wifi, Bluetooth, Ethernet and Low Power support all in a single chip. (vanepp) made breadboard work, adjusted pin numbering and labels and reduced size of schematic and cleaned up pcb. This chip is 30pins long (2 x15) and 11 pins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
