# Fritzing sketch ControlPaty (saved by Fritzing 1.0.1rc)
circuit board: 5.9cm x 5cm
breadboards: 1

parts:
  B_G = Pushbutton [part_number=B_Grabando package="[THT]"]
  L_G = LED - 5mm [color="Red (635nm)" current=0.030A part_number=L_Granbado package="5 mm [THT]"]
  R_G = Resistor [tolerance=±5% power=0.25W resistance=330 package=THT]
  R_BG = Resistor [tolerance=±5% power=0.25W resistance=10k package=THT]
  B_V = Pushbutton [part_number=B_Envivo package="[THT]"]
  L_V = LED - 5mm [color="Blue (430nm)" current=0.030A part_number=L_EnVivo package="5 mm [THT]"]
  R_V = Resistor [tolerance=±5% power=0.25W resistance=330 package=THT]
  R_BV = Resistor [tolerance=±5% power=0.25W resistance=10k package=THT]
  L_E = LED - 5mm [color="Yellow (592nm)" current=0.030A part_number=L_Estado package="5 mm [THT]"]
  R_E = Resistor [tolerance=±5% power=0.25W resistance=330 package=THT]
  ESP8266 = Amica NodeMCU DEVKIT 1.0
  OLED = OLED 128x64 I2C Monochrome Display GND-VDD

nets:
  3.3V: B_G.Pin_1, B_G.Pin_2, B_V.Pin_1, B_V.Pin_2, ESP8266.pin1, ESP8266.pin_10, ESP8266.pin_26
  D7: B_G.Pin_3, B_G.Pin_4, R_BG.Pin_1, ESP8266.pin6
  N1: L_G.cathode, R_G.Pin_1
  GND: L_G.anode, R_BG.Pin_0, L_V.anode, R_BV.Pin_0, L_E.anode, ESP8266.pin2, ESP8266.pin_9, ESP8266.pin_25, ESP8266.pin_29, OLED.GND
  D5: R_G.Pin_0, ESP8266.pin8
  D6: B_V.Pin_3, B_V.Pin_4, R_BV.Pin_1, ESP8266.pin7
  N2: L_V.cathode, R_V.Pin_1
  D3: R_V.Pin_0, ESP8266.pin_12
  N3: L_E.cathode, R_E.Pin_1
  D8: R_E.Pin_0, ESP8266.pin5
  SDA: ESP8266.pin_13, OLED.SDA
  SLK: ESP8266.pin_14, OLED.SCK
  5V: ESP8266.pin_30, OLED.VDD

custom parts:
  OLED 128x64 I2C Monochrome Display GND-VDD: OLED 128x64 I2C Monochrome Display. Note: there are two variants of this part, this one is the GND VDD SCK SDA variant. The other is VDD GND SCK SDA. Make sure you select the part that matches your module as using the incorrect part will probably destroy your module! In addition the mounting holes are marked on silkscreen but not by default drilled. If you want drilled mounting holes, copy a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
