# Fritzing sketch botonmusic (saved by Fritzing 1.0.1rc)
breadboards: 1

parts:
  M1 = DOIT Esp32 DevKit v1 (30 pins long, 11 pins width) [part_number=ESP32S-PIN30]
  R1 = Resistor [tolerance=±5% power=0.25W resistance=10k package=THT]
  S1 = Pushbutton [package="[THT]"]
  LED1 = LED - 5mm [color="Red (633nm)" current=0.030A package="5 mm [THT]"]
  R2 = Resistor [tolerance=±5% power=0.25W resistance=10k package=THT]
  S2 = Pushbutton [package="[THT]"]
  R3 = Resistor [tolerance=±5% power=0.25W resistance=10k package=THT]
  S3 = Pushbutton [package="[THT]"]
  R4 = Resistor [tolerance=±5% power=0.25W resistance=10k package=THT]
  S4 = Toggle Switch [package=THT]
  J1 = female pin header, 2 pins [form="♀ (female)"]

nets:
  N1: M1.3V3, R2.Pin_0, R3.Pin_0, R4.Pin_0
  N2: M1.GND, LED1.anode, S2.Pin_1, S2.Pin_2, S3.Pin_1, S3.Pin_2, S4.COM
  N3: M1.D15, S2.Pin_3, S2.Pin_4, R3.Pin_1
  N4: M1.D4, R1.Pin_0
  N5: M1.RX2, S1.Pin_3, S1.Pin_4, R2.Pin_1
  N6: M1.D5, S3.Pin_3, S3.Pin_4, R4.Pin_1
  N7: M1.VIN, J1.pin1
  N8: R1.Pin_1, LED1.cathode
  N9: S1.Pin_1, S1.Pin_2
  N10: S4.L1, J1.pin2

custom parts:
  DOIT Esp32 DevKit v1 (30 pins long, 11 pins width): The DOIT Esp32 DevKit v1 is one of the development board created by DOIT to evaluate the ESP-WROOM-32 module. It is based on the ESP32 microcontroller that boasts Wifi, Bluetooth, Ethernet and Low Power support all in a single chip. (vanepp) made breadboard work, adjusted pin numbering and labels and reduced size of schematic and cleaned up pcb. This chip is 30pins long (2 x15) and 11 pins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
